// Logisim project alu.circ as structural Verilog: 11 circuits, main circuit add
module main (
  input  [15:0] in_1,
  input  [15:0] in_2,
  input  [3:0] Switch,
  output Signed_Overflow,
  output [15:0] out_5,
  output Equal
);

  wire addOverflow, addp8Overflow, subOverflow, subp8Overflow;
  wire [15:0] add_1_out_3, addp8_1_out_3, and_1_out, or_1_out, sll_1_out_3, slt_1_out_3, sra_1_out_3,
       srl_1_out_3, sub_1_out_3, subp8_1_out_3;

  add add_1 (.in_1(in_1), .in_2(in_2), .out_3(add_1_out_3), .out_4(addOverflow));
  sub sub_1 (.in_1(in_1), .in_2(in_2), .out_3(sub_1_out_3), .out_4(subOverflow));
  sll sll_1 (.in_1(in_1), .in_2(in_2), .out_3(sll_1_out_3));
  srl srl_1 (.in_1(in_1), .in_2(in_2), .out_3(srl_1_out_3));
  sra sra_1 (.in_1(in_1), .in_2(in_2), .out_3(sra_1_out_3));
  slt slt_1 (.in_1(in_1), .in_2(in_2), .out_3(slt_1_out_3));
  assign or_1_out = in_1 | in_2;  // OR_Gate or_1, 16 bits wide
  assign and_1_out = in_1 & in_2;  // AND_Gate and_1, 16 bits wide
  addp8 addp8_1 (.in_1(in_1), .in_2(in_2), .out_3(addp8_1_out_3), .out_4(addp8Overflow));
  subp8 subp8_1 (.in_1(in_1), .in_2(in_2), .out_3(subp8_1_out_3), .out_4(subp8Overflow));
  Multiplexer #(.select(4), .width(16), .enable("false")) multiplexer_1 (
    .in0(add_1_out_3), .in1(sub_1_out_3), .in2(sll_1_out_3), .in3(srl_1_out_3), .in4(sra_1_out_3),
    .in5(slt_1_out_3), .in6(or_1_out), .in7(and_1_out), .in8(addp8_1_out_3), .in9(subp8_1_out_3),
    .out(out_5), .sel(Switch));  // open: in10, in11, in12, in13, in14, in15
  Multiplexer #(.select(4), .enable("false")) multiplexer_2 (
    .in0(addOverflow), .in1(subOverflow), .in2(1'b0), .in3(1'b0), .in4(1'b0), .in5(1'b0), .in6(1'b0),
    .in7(1'b0), .in8(addp8Overflow), .in9(subp8Overflow), .out(Signed_Overflow), .sel(Switch));  // open: in10, in11, in12, in13, in14, in15
  Comparator #(.width(16)) comparator_1 (.a(in_1), .b(in_2), .eq(Equal));  // open: gt, lt

  // Other names for the same wires on the sheet: out[15:0] = out_5; overflow = Signed_Overflow; S[3:0] = Switch;
  //   X[15:0] = in_1; Y[15:0] = in_2

  // Notes on the sheet:
  //   INPUTS
endmodule

module add (
  input  [15:0] in_1,
  input  [15:0] in_2,
  output [15:0] out_3,
  output out_4
);

  wire and_1_out, and_2_out;

  Adder #(.width(16)) adder_1 (.a(in_1), .b(in_2), .out(out_3));  // open: cin, cout
  and and_1 (and_1_out, in_1[15], in_2[15], ~out_3[15]);  // AND_Gate
  and and_2 (and_2_out, ~in_1[15], ~in_2[15], out_3[15]);  // AND_Gate
  or or_1 (out_4, and_1_out, and_2_out);

  // Other names for the same wires on the sheet: out[15:0] = out_3; MSB3 = out_3[15]; signedOverflow = out_4;
  //   X[15:0] = in_1; MSB1 = in_1[15]; Y[15:0] = in_2; MSB2 = in_2[15]

  // Notes on the sheet:
  //   positive + positive = negative
  //   negative + negative = postive
endmodule

module sub (
  input  [15:0] in_1,
  input  [15:0] in_2,
  output [15:0] out_3,
  output out_4
);

  wire and_1_out, and_2_out;

  Subtractor #(.width(16)) subtractor_1 (.a(in_1), .b(in_2), .out(out_3));  // open: bin, bout
  and and_1 (and_1_out, ~in_1[15], in_2[15], out_3[15]);  // AND_Gate
  and and_2 (and_2_out, in_1[15], ~in_2[15], ~out_3[15]);  // AND_Gate
  or or_1 (out_4, and_1_out, and_2_out);

  // Other names for the same wires on the sheet: out[15:0] = out_3; MSB3 = out_3[15]; signedOverflow = out_4;
  //   X[15:0] = in_1; MSB1 = in_1[15]; Y[15:0] = in_2; MSB2 = in_2[15]

  // Notes on the sheet:
  //   negative - postive = positive
  //   positive - negative = negative
endmodule

module sll (
  input  [15:0] in_1,
  input  [15:0] in_2,
  output [15:0] out_3
);

  Shifter #(.width(16)) shifter_1 (.in(in_1), .\dist (in_2[3:0]), .out(out_3));

  // Other names for the same wires on the sheet: out[15:0] = out_3; X[15:0] = in_1; Y[15:0] = in_2
endmodule

module srl (
  input  [15:0] in_1,
  input  [15:0] in_2,
  output [15:0] out_3
);

  Shifter #(.width(16), .shift("lr")) shifter_1 (.in(in_1), .\dist (in_2[3:0]), .out(out_3));

  // Other names for the same wires on the sheet: out[15:0] = out_3; X[15:0] = in_1; Y[15:0] = in_2
endmodule

module sra (
  input  [15:0] in_1,
  input  [15:0] in_2,
  output [15:0] out_3
);

  Shifter #(.width(16), .shift("ar")) shifter_1 (.in(in_1), .\dist (in_2[3:0]), .out(out_3));

  // Other names for the same wires on the sheet: out[15:0] = out_3; X[15:0] = in_1; Y[15:0] = in_2
endmodule

module slt (
  input  [15:0] in_1,
  input  [15:0] in_2,
  output [15:0] out_3
);

  wire comparator_1_lt;

  Comparator #(.width(16)) comparator_1 (.a(in_1), .b(in_2), .lt(comparator_1_lt));  // open: gt, eq
  assign out_3 = {{15{1'b0}}, comparator_1_lt};  // Bit_Extender bit_extender_1

  // Other names for the same wires on the sheet: out[15:0] = out_3; X[15:0] = in_1; Y[15:0] = in_2
endmodule

module addp8 (
  input  [15:0] in_1,
  input  [15:0] in_2,
  output [15:0] out_3,
  output out_4
);

  wire add8_1_out_4, add8_2_out_4;

  add8 add8_1 (.in_1(in_1[7:0]), .in_2(in_2[7:0]), .out_3(out_3[7:0]), .out_4(add8_1_out_4));
  add8 add8_2 (.in_1(in_1[15:8]), .in_2(in_2[15:8]), .out_3(out_3[15:8]), .out_4(add8_2_out_4));
  or or_1 (out_4, add8_1_out_4, add8_2_out_4);

  // Other names for the same wires on the sheet: out[15:0] = out_3; signedOverflow = out_4; X[15:0] = in_1;
  //   Y[15:0] = in_2
endmodule

module subp8 (
  input  [15:0] in_1,
  input  [15:0] in_2,
  output [15:0] out_3,
  output out_4
);

  wire sub8_1_out_4, sub8_2_out_4;

  sub8 sub8_1 (.in_1(in_1[7:0]), .in_2(in_2[7:0]), .out_3(out_3[7:0]), .out_4(sub8_1_out_4));
  sub8 sub8_2 (.in_1(in_1[15:8]), .in_2(in_2[15:8]), .out_3(out_3[15:8]), .out_4(sub8_2_out_4));
  or or_1 (out_4, sub8_1_out_4, sub8_2_out_4);

  // Other names for the same wires on the sheet: out[15:0] = out_3; signedOverflow = out_4; X[15:0] = in_1;
  //   Y[15:0] = in_2
endmodule

module add8 (
  input  [7:0] in_1,
  input  [7:0] in_2,
  output [7:0] out_3,
  output out_4
);

  wire and_1_out, and_2_out;

  Adder adder_1 (.a(in_1), .b(in_2), .out(out_3));  // open: cin, cout
  and and_1 (and_1_out, in_1[7], in_2[7], ~out_3[7]);  // AND_Gate
  and and_2 (and_2_out, ~in_1[7], ~in_2[7], out_3[7]);  // AND_Gate
  or or_1 (out_4, and_1_out, and_2_out);

  // Other names for the same wires on the sheet: out[7:0] = out_3; MSB3 = out_3[7]; signedOverflow = out_4;
  //   X[7:0] = in_1; MSB1 = in_1[7]; Y[7:0] = in_2; MSB2 = in_2[7]

  // Notes on the sheet:
  //   positive + positive = negative
  //   negative + negative = postive
endmodule

module sub8 (
  input  [7:0] in_1,
  input  [7:0] in_2,
  output [7:0] out_3,
  output out_4
);

  wire and_1_out, and_2_out;

  Subtractor subtractor_1 (.a(in_1), .b(in_2), .out(out_3));  // open: bin, bout
  and and_1 (and_1_out, ~in_1[7], in_2[7], out_3[7]);  // AND_Gate
  and and_2 (and_2_out, in_1[7], ~in_2[7], ~out_3[7]);  // AND_Gate
  or or_1 (out_4, and_1_out, and_2_out);

  // Other names for the same wires on the sheet: out[7:0] = out_3; MSB3 = out_3[7]; signedOverflow = out_4;
  //   X[7:0] = in_1; MSB1 = in_1[7]; Y[7:0] = in_2; MSB2 = in_2[7]

  // Notes on the sheet:
  //   negative - postive = positive
  //   positive - negative = negative
endmodule
