// Logisim project cpu.circ as structural Verilog: 3 circuits, main circuit main
module main (
  input  [15:0] From_Instr_Mem,
  input  clk,
  output [15:0] r0,
  output [15:0] r1,
  output [15:0] r2,
  output [15:0] r3,
  output [15:0] Display_0,
  output [15:0] Display_1,
  output [15:0] To_Instr_Mem,
  output [15:0] Data_Mem_Data,
  output [15:0] Data_Mem_Addr,
  output Data_Mem_Write
);

  wire ALUsrc, branch, button_1_out, disp, enable0, enable1, eqInvert, equal, j, jal, jr, lui,
       main_1_signed_overflow, MemToReg, nop, not_1_out, regDst, regWrite, zeroExtend;
  wire [1:0] multiplexer_6_out, multiplexer_8_out;
  wire [3:0] ALUctr;
  wire [11:0] address, register_3_q;
  wire [15:0] bit_extender_1_out, bit_extender_2_out, controlled_buffer_1_out, immExtended, main_1_out_5,
       memOut, multiplexer_2_out, multiplexer_3_out, multiplexer_7_out, multiplexer_9_out, \output , output2,
       R_rs, shifter_1_out, sum, sum2;
  wire [15:12] in, instr;

  Multiplexer #(.width(16), .enable("false")) multiplexer_1 (.in0(output2), .in1(R_rs), .out(\output ), .sel(jr));
  Multiplexer #(.width(16), .enable("false")) multiplexer_2 (
    .in0(sum), .in1(\output ), .out(multiplexer_2_out), .sel(nop));
  nop nop_1 (.j(j), .jr(jr), .eqInvert(eqInvert), .equal(equal), .branch(branch), .nop(nop));
  Adder #(.width(16)) adder_1 (.a(16'h1), .b(To_Instr_Mem), .out(sum));  // open: cin, cout
  Register #(.width(16)) register_1 (.D(multiplexer_2_out), .Q(To_Instr_Mem), .clk(clk));  // open: en, clr
  Multiplexer #(.width(16), .enable("false")) multiplexer_3 (
    .in0(From_Instr_Mem), .in1(16'h6), .out(multiplexer_3_out), .sel(nop));
  control control_1 (
    .in_1(instr), .in_2(address[5:0]), .regDst(regDst), .ALUsrc(ALUsrc), .MemToReg(MemToReg),
    .regWrite(regWrite), .memWrite(Data_Mem_Write), .jr(jr), .j(j), .jal(jal), .eqInvert(eqInvert),
    .branch(branch), .lui(lui), .ALUctr1(ALUctr[1:0]), .ALUctr2(ALUctr[3:2]), .zeroExtend(zeroExtend),
    .disp(disp));
  Register #(.width(16)) register_2 (.D(multiplexer_3_out), .Q({instr, address}), .clk(clk));  // open: en, clr
  Register #(.width(16)) register_3 (.D(To_Instr_Mem), .Q({in, register_3_q}), .clk(clk));  // open: en, clr
  Multiplexer #(.width(16), .enable("false")) multiplexer_4 (.in0(sum2), .in1({in, address}), .out(output2), .sel(j));
  Adder #(.width(16)) adder_2 (.a(immExtended), .b(To_Instr_Mem), .out(sum2));  // open: cin, cout
  Multiplexer #(.width(16), .enable("false")) multiplexer_5 (
    .in0(bit_extender_1_out), .in1(bit_extender_2_out), .out(immExtended), .sel(zeroExtend));
  assign bit_extender_1_out = {{8{address[7]}}, address[7:0]};  // Bit_Extender bit_extender_1
  assign bit_extender_2_out = {{8{1'b0}}, address[7:0]};  // Bit_Extender bit_extender_2
  Multiplexer #(.width(2), .enable("false")) multiplexer_6 (
    .in0(address[9:8]), .in1(address[7:6]), .out(multiplexer_6_out), .sel(regDst));
  Multiplexer #(.width(16), .enable("false")) multiplexer_7 (
    .in0(Data_Mem_Data), .in1(immExtended), .out(multiplexer_7_out), .sel(ALUsrc));
  Multiplexer #(.width(2), .enable("false")) multiplexer_8 (
    .in0(multiplexer_6_out), .in1(2'b11), .out(multiplexer_8_out), .sel(jal));
  Multiplexer #(.width(16), .enable("false")) multiplexer_9 (
    .in0(memOut), .in1(To_Instr_Mem), .out(multiplexer_9_out), .sel(jal));
  LED led_1 (.in(main_1_signed_overflow));
  alu_main main_1 (
    .Switch(ALUctr), .in_1(R_rs), .Equal(equal), .out_5(main_1_out_5),
    .Signed_Overflow(main_1_signed_overflow), .in_2(multiplexer_7_out));
  Regfile_main main_2 (
    .Read_register_1(address[11:10]), .Read_register_2(address[9:8]), .write_register(multiplexer_8_out),
    .write_data(multiplexer_9_out), .Reg_0_Value(r0), .Reg_1_Value(r1), .Reg_2_Value(r2), .Reg_3_Value(r3),
    .RegWrite(regWrite), .clock(clk), .Read_Data_1(R_rs), .Read_Data_2(Data_Mem_Data));
  Shifter #(.width(16)) shifter_1 (.in(immExtended), .\dist (4'b1000), .out(shifter_1_out));
  Multiplexer #(.width(16), .enable("false")) multiplexer_10 (
    .in0(main_1_out_5), .in1(shifter_1_out), .out(Data_Mem_Addr), .sel(lui));
  Hex_Digit_Display hex_digit_display_1 (.value(Display_0[15:12]));  // open: dp
  Hex_Digit_Display hex_digit_display_2 (.value(Display_0[11:8]));  // open: dp
  Register #(.width(16)) register_4 (.D(R_rs), .en(enable0), .Q(Display_0), .clk(clk));  // open: clr
  Hex_Digit_Display hex_digit_display_3 (.value(Display_0[3:0]));  // open: dp
  Hex_Digit_Display hex_digit_display_4 (.value(Display_0[7:4]));  // open: dp
  Demultiplexer #(.enable("false")) demultiplexer_1 (.out0(enable0), .out1(enable1), .in(disp), .sel(address[0]));
  assign controlled_buffer_1_out = Data_Mem_Write ? Data_Mem_Data : 16'bz;  // Controlled_Buffer controlled_buffer_1
  RAM #(.addrWidth(16), .dataWidth(16)) ram_1 (
    .addr(Data_Mem_Addr), .data(controlled_buffer_1_out), .sel(1'b1), .clk(clk), .ld(not_1_out),
    .clr(button_1_out));
  not not_1 (not_1_out, Data_Mem_Write);
  Button button_1 (.out(button_1_out));
  Multiplexer #(.width(16), .enable("false")) multiplexer_11 (
    .in0(Data_Mem_Addr), .in1(controlled_buffer_1_out), .out(memOut), .sel(MemToReg));
  Hex_Digit_Display hex_digit_display_5 (.value(Display_1[15:12]));  // open: dp
  Hex_Digit_Display hex_digit_display_6 (.value(Display_1[11:8]));  // open: dp
  Register #(.width(16)) register_5 (.D(R_rs), .en(enable1), .Q(Display_1), .clk(clk));  // open: clr
  Hex_Digit_Display hex_digit_display_7 (.value(Display_1[7:4]));  // open: dp
  Hex_Digit_Display hex_digit_display_8 (.value(Display_1[3:0]));  // open: dp

  // Other names for the same wires on the sheet: ALUout[15:0] = Data_Mem_Addr; d0[15:0] = Display_0;
  //   d1[15:0] = Display_1; funct[5:0] = address[5:0]; imm[7:0] = address[7:0]; in[11:0] = address;
  //   instr[11:0] = address; rd[1:0] = address[7:6]; rt[1:0] = address[9:8]; rs[1:0] = address[11:10];
  //   opcode[3:0] = instr; memWrite = Data_Mem_Write; PC[15:0] = To_Instr_Mem; R_rt[15:0] = Data_Mem_Data

  // Notes on the sheet:
  //   This is a CLK that is an INPUT driven from the harness.
  //   Remember, this circuit is loaded from the harness to be tested!
  //   PC
  //   Control Unit
  //   DO NOT CHANGE THE LOCATIONS OF THE INPUTS OR OUTPUTS! IF YOU DO SO, YOU NEED TO MAKE SURE THE PINS ARE IN THE RIGHT PLACES!
  //   These are OUTPUTS of the circuit
  //   ALU
  //   Register
  //   These are OUTPUTS of the circuit
  //   Display
  //   Memory
endmodule

module control (
  input  [3:0] in_1,
  input  [5:0] in_2,
  output regDst,
  output ALUsrc,
  output MemToReg,
  output regWrite,
  output memWrite,
  output jr,
  output j,
  output jal,
  output eqInvert,
  output branch,
  output lui,
  output [1:0] ALUctr1,
  output [1:0] ALUctr2,
  output zeroExtend,
  output disp
);

  wire addi, andi, beq, j_t, not_1_out, not_2_out, not_3_out, ori;
  wire [2:1] out;

  Decoder #(.select(4), .enable("false")) decoder_1 (
    .out0(regDst), .out1(jal), .out2(j_t), .out3(jr), .out4(beq), .out5(addi), .out6(andi), .out7(ori),
    .out8(eqInvert), .out9(memWrite), .out10(lui), .out11(MemToReg), .out12(disp), .sel(in_1));  // open: out13, out14, out15
  or or_1 (out[2], andi, ori);
  or or_2 (out[1], andi, ori);
  not not_1 (not_1_out, beq);
  not not_2 (not_2_out, eqInvert);
  not not_3 (not_3_out, regDst);
  or or_3 (regWrite, regDst, andi, addi, MemToReg, lui, jal, ori);
  Multiplexer #(.width(4), .enable("false")) multiplexer_1 (
    .in0({1'b0, out, andi}), .in1(in_2[3:0]), .out({ALUctr2, ALUctr1}), .sel(regDst));
  and and_1 (ALUsrc, not_1_out, not_2_out, not_3_out);
  or or_4 (j, j_t, jal);
  or or_5 (branch, beq, eqInvert);
  or or_6 (zeroExtend, andi, ori, lui, disp);

  // Other names for the same wires on the sheet: bne = eqInvert; funct[3:0] = in_2[3:0]; lw = MemToReg;
  //   opcode[3:0] = in_1; out[0] = andi; rType = regDst; sw = memWrite

  // Notes on the sheet:
  //   regWrite
endmodule

module nop (
  input  eqInvert,
  input  jr,
  input  equal,
  input  branch,
  input  j,
  output nop
);

  wire and_1_out, or_1_out, xor_1_out;

  or or_1 (or_1_out, j, jr);
  or or_2 (nop, or_1_out, and_1_out);
  and and_1 (and_1_out, xor_1_out, branch);
  xor xor_1 (xor_1_out, eqInvert, equal);
endmodule
